# Fritzing sketch SF51-Living-Light (saved by Fritzing 0.9.3b)
breadboards: 1

parts:
  HLK-PM1 = HLK-PM01
  BULB1 = Incandescent light bulb small [package="bulb sm"]
  KY-1 = Keyes Relay [package=THT]
  TTP223B1 = TTP223B Capacitive Touch Sensor Module
  U7 = NodeMCU V3.0
  KY-2 = Keyes Relay [package=THT]
  BULB2 = Incandescent light bulb small [package="bulb sm"]
  TTP223B2 = TTP223B Capacitive Touch Sensor Module

nets:
  N1: HLK-PM1.AC#0, BULB1.1, BULB2.1
  N2: HLK-PM1.AC#1, KY-1.C, KY-2.C
  N3: HLK-PM1.-Vo, U7.GND#6, U7.GND#13, U7.GND#16, U7.GND#33
  N4: HLK-PM1.+Vo, U7.Vin
  N5: BULB1.2, KY-1.NO
  N6: KY-1.signal, U7.D6
  N7: KY-1.power, KY-2.power
  GND: KY-1.ground, TTP223B1.GND, KY-2.ground, TTP223B2.GND
  VCC: TTP223B1.VCC, U7.3V3, TTP223B2.VCC
  N8: TTP223B1.SIG, U7.D1
  N9: U7.D2, TTP223B2.SIG
  N10: U7.D7, KY-2.signal
  N11: KY-2.NO, BULB2.2

custom parts:
  Keyes Relay: The Keyes 5V relay module is suitable for SCM development, home appliance control. It uses a 5V~12V TIL control signal which can control DC / AC signal.
  TTP223B Capacitive Touch Sensor Module: The TTP223B capacitive touch sensor module uses the TTP223B IC. The appropriate voltage is approximately 2 to 5.5 volts.
  NodeMCU V3.0: ESP8266 based NodeMCU
